# Fritzing sketch BreadboardLayout (saved by Fritzing 0.8.3b)
breadboards: 1

parts:
  U1 = ESP8266 WiFi Module [part_number=ESP8266]
  IC1 = Voltage Regulator [package=to-92]
  KY-1 = Keyes Relay [package=THT]
  R1 = Resistor [tolerance=±5% resistance=220 package=THT]
  C1 = Electrolytic Capacitor [capacitance=100µF voltage=16V package="200 mil [THT, electrolytic]"]
  C2 = Ceramic Capacitor [capacitance=100nF package="100 mil [THT, multilayer]"]
  Power_plug1 = Power plug
  Digispark1 = Digispark
  R2 = Resistor [tolerance=±5% resistance=1k package=THT]
  R3 = Resistor [tolerance=±5% resistance=1k package=THT]
  UDS1 = PING Ultrasonic Sensor

nets:
  N1: U1.RXD, R2.Pin_0
  N2: U1.VCC, U1.CH_PD, IC1.OUT, C1.+, C2.1
  N3: U1.GPIO_2, R1.Pin_0
  GND: U1.GND, IC1.GND, KY-1.ground, C1.-, C2.0, Power_plug1.GND, Digispark1.GND, R3.Pin_0, UDS1.GND
  VCC: IC1.IN, KY-1.power, Power_plug1.VCC, Digispark1.VCC, UDS1.VCC
  N4: KY-1.signal, R1.Pin_1
  N5: Digispark1.P1, R2.Pin_1, R3.Pin_1
  N6: Digispark1.P2, UDS1.I/O

notes:
  I cannot find correct vReg in Fritzing - the vReg that I use has the pinout of Gnd, In, Out from left to right. I'll be showing my pinout here even though this regulator has different pins.
  These wires go to the garage door opener
  5V USB Power

custom parts:
  ESP8266 WiFi Module: Generic WiFi Module based on the ESP8266 with onboard PCB antenna and UART communications
  Keyes Relay: The Keyes 5V relay module is suitable for SCM development, home appliance control. It uses a 5V~12V TIL control signal which can control DC / AC signal.
  Digispark: The Digispark is an Attiny85 based microcontroller development board similar to the Arduino line, only cheaper, smaller, and a bit less powerful. With a whole host of shields to extend its functionality and the ability to use the familiar Arduino IDE the Digispark is a great way to jump into electronics, or perfect for when an Arduino is too big or too much.
  PING Ultrasonic Sensor: The PING)))™ ultrasonic sensor provides an easy method of distance measurement. This sensor is perfect for any number of applications that require you to perform measurements between moving or stationary objects. Interfacing to a microcontroller is a snap. A single I/O pin is used to trigger an ultrasonic burst (well above human hearing) and then "listen" for the echo return pulse. The sensor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
